// Logisim project p_208.circ as structural Verilog: 1 circuit, main circuit main
module main (
);

  wire Clear_out, clock_1_out;
  wire [7:0] adder_1_out, ram_1_data, register_1_q;
  wire [15:0] counter_1_q;

  Clock clock_1 (.out(clock_1_out));
  Button Clear (.out(Clear_out));
  Counter #(.width(16), .max('hffff)) counter_1 (
    .Q(counter_1_q), .clk(clock_1_out), .clr(Clear_out));  // open: load, D, count, carry
  RAM #(.addrWidth(16)) ram_1 (.addr(counter_1_q), .data(ram_1_data), .clk(clock_1_out));  // open: sel, ld, clr
  Adder adder_1 (.a(ram_1_data), .b(register_1_q), .out(adder_1_out));  // open: cin, cout
  Register register_1 (.D(adder_1_out), .Q(register_1_q), .clk(clock_1_out), .clr(Clear_out));  // open: en
  // Probe on register_1_q
endmodule
