// Logisim project p_214.circ as structural Verilog: 3 circuits, main circuit main
module main (
);

  wire adder_1_cout, and_2_out, and_3_out, clk, clock_1_out, multiplexer_2_out, op_decoder_1_add,
       op_decoder_1_hold, op_decoder_1_load, op_decoder_1_store, op_decoder_1_subtract,
       op_decoder_1_with_carry, or_1_out, or_2_out, register_1_q, rst_out;
  wire [7:0] adder_1_out, multiplexer_1_out, multiplexer_3_out, not_1_out, ram_1_data, ram_2_data,
       register_2_q;
  wire [15:0] counter_1_q;

  Counter #(.width(16), .max('hffff)) counter_1 (
    .Q(counter_1_q), .clk(clk), .clr(rst_out));  // open: load, D, count, carry
  Button rst (.out(rst_out));
  RAM #(.addrWidth(16)) ram_1 (.addr(counter_1_q), .data(ram_1_data), .clk(clk));  // open: sel, ld, clr
  RAM #(.addrWidth(16), .bus("separate")) ram_2 (
    .addr(counter_1_q), .din(register_2_q), .data(ram_2_data), .str(op_decoder_1_store), .clk(clk));  // open: sel, ld, clr
  Clock clock_1 (.out(clock_1_out));
  Op_decoder op_decoder_1 (
    .opcode(ram_1_data), .Load(op_decoder_1_load), .Store(op_decoder_1_store), .Add(op_decoder_1_add),
    .With_carry(op_decoder_1_with_carry), .Subtract(op_decoder_1_subtract), .Hold(op_decoder_1_hold));
  assign not_1_out = ~ram_2_data;  // NOT_Gate not_1, 8 bits wide
  Multiplexer #(.width(8)) multiplexer_1 (
    .in0(ram_2_data), .in1(not_1_out), .out(multiplexer_1_out), .sel(op_decoder_1_subtract));
  and and_1 (clk, clock_1_out, ~op_decoder_1_hold);  // AND_Gate
  Multiplexer multiplexer_2 (
    .in0(op_decoder_1_subtract), .in1(register_1_q), .out(multiplexer_2_out), .sel(op_decoder_1_with_carry));
  // Probe on adder_1_out
  Adder adder_1 (
    .a(register_2_q), .b(multiplexer_1_out), .out(adder_1_out), .cin(multiplexer_2_out), .cout(adder_1_cout));
  Register #(.width(1)) register_1 (.D(adder_1_cout), .Q(register_1_q), .clk(and_2_out), .clr(rst_out));  // open: en
  or or_1 (or_1_out, op_decoder_1_subtract, op_decoder_1_add);
  Multiplexer #(.width(8)) multiplexer_3 (.in0(ram_2_data), .in1(adder_1_out), .out(multiplexer_3_out), .sel(or_1_out));
  and and_2 (and_2_out, or_1_out, ~clk);  // AND_Gate
  or or_2 (or_2_out, op_decoder_1_subtract, op_decoder_1_add, op_decoder_1_load);
  Register register_2 (.D(multiplexer_3_out), .Q(register_2_q), .clk(and_3_out), .clr(rst_out));  // open: en
  and and_3 (and_3_out, or_2_out, ~clk);  // AND_Gate

  // Notes on the sheet:
  //   Code
  //   Data
endmodule

module Op_decoder (
  input  [7:0] opcode,
  output Load,
  output Store,
  output Add,
  output With_carry,
  output Subtract,
  output Hold
);

  wire equator_3_output, equator_4_output, equator_5_output, equator_6_output;

  equator equator_1 (.value1(8'h10), .value2(opcode), .\output (Load));
  equator equator_2 (.value1(8'h11), .value2(opcode), .\output (Store));
  equator equator_3 (.value1(8'h20), .value2(opcode), .\output (equator_3_output));
  equator equator_4 (.value1(8'h22), .value2(opcode), .\output (equator_4_output));
  equator equator_5 (.value1(8'h21), .value2(opcode), .\output (equator_5_output));
  equator equator_6 (.value1(8'h23), .value2(opcode), .\output (equator_6_output));
  equator equator_7 (.value1({8{1'b1}}), .value2(opcode), .\output (Hold));
  or or_1 (Add, equator_3_output, equator_4_output);
  or or_2 (Subtract, equator_5_output, equator_6_output);
  or or_3 (With_carry, equator_4_output, equator_6_output);
endmodule

module equator (
  input  [7:0] value1,
  input  [7:0] value2,
  output \output 
);

  wire [7:0] xnor_1_out;

  assign xnor_1_out = ~(value1 ^ value2);  // XNOR_Gate xnor_1, 8 bits wide
  and and_1 (\output , xnor_1_out[0], xnor_1_out[1], xnor_1_out[2], xnor_1_out[3], xnor_1_out[4], xnor_1_out[5], xnor_1_out[6], xnor_1_out[7]);
endmodule
