// Logisim project p_222_test.circ as structural Verilog: 2 circuits, main circuit main
module main (
);

  wire clock_1_out, equator_1_output, equator_2_output, equator_3_output, equator_4_output, rst_out;
  wire [1:0] counter_2_q;
  wire [7:0] ram_1_data, register_1_q, register_2_q, register_3_q;
  wire [15:0] counter_1_q, multiplexer_1_out;

  Counter #(.width(16), .max('hffff)) counter_1 (
    .Q(counter_1_q), .clk(clock_1_out), .clr(rst_out));  // open: load, D, count, carry
  Clock clock_1 (.out(clock_1_out));
  Button rst (.out(rst_out));
  Multiplexer #(.width(16)) multiplexer_1 (
    .in0(counter_1_q), .in1({register_2_q, register_3_q}), .out(multiplexer_1_out), .sel(equator_4_output));
  RAM #(.addrWidth(16)) ram_1 (.addr(multiplexer_1_out), .data(ram_1_data), .clk(clock_1_out));  // open: sel, ld, clr
  Counter #(.width(2), .max('h3)) counter_2 (
    .Q(counter_2_q), .clk(clock_1_out), .clr(rst_out));  // open: load, D, count, carry
  equator equator_1 (.value1(2'b00), .value2(counter_2_q), .\output (equator_1_output));
  equator equator_2 (.value1(2'b01), .value2(counter_2_q), .\output (equator_2_output));
  equator equator_3 (.value1(2'b10), .value2(counter_2_q), .\output (equator_3_output));
  equator equator_4 (.value1(2'b11), .value2(counter_2_q), .\output (equator_4_output));
  Register #(.trigger("falling")) register_1 (
    .D(ram_1_data), .Q(register_1_q), .clk(equator_1_output), .clr(rst_out));  // open: en
  Register #(.trigger("falling")) register_2 (
    .D(ram_1_data), .Q(register_2_q), .clk(equator_2_output), .clr(rst_out));  // open: en
  Register #(.trigger("falling")) register_3 (
    .D(ram_1_data), .Q(register_3_q), .clk(equator_3_output), .clr(rst_out));  // open: en
endmodule

module equator (
  input  [1:0] value1,
  input  [1:0] value2,
  output \output 
);

  wire [1:0] xnor_1_out;

  assign xnor_1_out = ~(value1 ^ value2);  // XNOR_Gate xnor_1, 2 bits wide
  and and_1 (\output , xnor_1_out[0], xnor_1_out[1]);
endmodule
