// Logisim project p_227.circ as structural Verilog: 5 circuits, main circuit main
module main (
);

  wire adder_1_cout, addr_clk, and_1_out, and_2_out, and_3_out, and_5_out, and_6_out, clk, clock_1_out,
       multiplexer_1_out, multiplexer_4_out, n2bit_equator_1_output, n2bit_equator_2_output,
       n2bit_equator_3_output, not_1_out, op_decoder_1_add, op_decoder_1_hold, op_decoder_1_jump,
       op_decoder_1_load, op_decoder_1_store, op_decoder_1_subtract, op_decoder_1_with_carry, or_1_out,
       or_2_out, or_3_out, register_1_q, register_7_q, rst_out;
  wire [1:0] counter_2_q;
  wire [7:0] adder_1_out, multiplexer_3_out, multiplexer_5_out, not_2_out, ram_1_data, register_2_q,
       register_3_q, register_4_q, register_5_q, register_6_q, register_8_q;
  wire [15:0] counter_1_value, multiplexer_2_out;

  Multiplexer multiplexer_1 (.in0(and_1_out), .in1(not_1_out), .out(multiplexer_1_out), .sel(and_2_out));
  not not_1 (not_1_out, and_1_out);
  counter counter_1 (
    .Set_value({register_3_q, register_4_q}), .Set(and_2_out), .Clock(multiplexer_1_out), .Reset(rst_out),
    .Value(counter_1_value));
  and and_1 (and_1_out, addr_clk, ~register_1_q);  // AND_Gate
  Button rst (.out(rst_out));
  // Probe on counter_1_value
  Multiplexer #(.width(16)) multiplexer_2 (
    .in0(counter_1_value), .in1({register_3_q, register_4_q}), .out(multiplexer_2_out), .sel(or_1_out));
  or or_1 (or_1_out, clk, and_3_out);
  Register #(.width(1), .trigger("falling")) register_1 (
    .D(clk), .Q(register_1_q), .clk(addr_clk), .clr(rst_out));  // open: en
  RAM #(.addrWidth(16), .bus("separate")) ram_1 (
    .addr(multiplexer_2_out), .din(register_8_q), .data(ram_1_data), .str(and_3_out), .clk(addr_clk));  // open: sel, ld, clr
  and and_2 (and_2_out, op_decoder_1_jump, clk);
  _2bit_equator u_2bit_equator_1 (.value1(2'b00), .value2(counter_2_q), .\output (n2bit_equator_1_output));
  _2bit_equator u_2bit_equator_2 (.value1(2'b01), .value2(counter_2_q), .\output (n2bit_equator_2_output));
  Counter #(.width(2), .max('h3)) counter_2 (
    .Q(counter_2_q), .clk(addr_clk), .clr(rst_out));  // open: load, D, count, carry
  _2bit_equator u_2bit_equator_3 (.value1(2'b10), .value2(counter_2_q), .\output (n2bit_equator_3_output));
  _2bit_equator u_2bit_equator_4 (.value1(2'b11), .value2(counter_2_q), .\output (clk));
  Register #(.trigger("falling")) register_2 (
    .D(ram_1_data), .Q(register_2_q), .clk(n2bit_equator_1_output), .clr(rst_out));  // open: en
  Register #(.trigger("falling")) register_3 (
    .D(ram_1_data), .Q(register_3_q), .clk(n2bit_equator_2_output), .clr(rst_out));  // open: en
  Register #(.trigger("falling")) register_4 (
    .D(ram_1_data), .Q(register_4_q), .clk(n2bit_equator_3_output), .clr(rst_out));  // open: en
  Register #(.trigger("high")) register_5 (.D(register_2_q), .Q(register_5_q), .clk(clk), .clr(rst_out));  // open: en
  Register #(.trigger("high")) register_6 (.D(ram_1_data), .Q(register_6_q), .clk(clk), .clr(rst_out));  // open: en
  and and_3 (and_3_out, clk, op_decoder_1_store);
  Clock clock_1 (.out(clock_1_out));
  Op_decoder op_decoder_1 (
    .opcode(register_5_q), .Load(op_decoder_1_load), .Store(op_decoder_1_store), .Add(op_decoder_1_add),
    .With_carry(op_decoder_1_with_carry), .Subtract(op_decoder_1_subtract), .Jump(op_decoder_1_jump),
    .Hold(op_decoder_1_hold));
  assign not_2_out = ~register_6_q;  // NOT_Gate not_2, 8 bits wide
  Multiplexer #(.width(8)) multiplexer_3 (
    .in0(register_6_q), .in1(not_2_out), .out(multiplexer_3_out), .sel(op_decoder_1_subtract));
  and and_4 (addr_clk, clock_1_out, ~op_decoder_1_hold);  // AND_Gate
  Multiplexer multiplexer_4 (
    .in0(op_decoder_1_subtract), .in1(register_7_q), .out(multiplexer_4_out), .sel(op_decoder_1_with_carry));
  Adder adder_1 (
    .a(register_8_q), .b(multiplexer_3_out), .out(adder_1_out), .cin(multiplexer_4_out), .cout(adder_1_cout));
  // Probe on adder_1_out
  Register #(.width(1)) register_7 (.D(adder_1_cout), .Q(register_7_q), .clk(and_5_out), .clr(rst_out));  // open: en
  or or_2 (or_2_out, op_decoder_1_subtract, op_decoder_1_add);
  Multiplexer #(.width(8)) multiplexer_5 (
    .in0(register_6_q), .in1(adder_1_out), .out(multiplexer_5_out), .sel(or_2_out));
  and and_5 (and_5_out, or_2_out, ~clk);  // AND_Gate
  or or_3 (or_3_out, op_decoder_1_subtract, op_decoder_1_add, op_decoder_1_load);
  Register register_8 (.D(multiplexer_5_out), .Q(register_8_q), .clk(and_6_out), .clr(rst_out));  // open: en
  and and_6 (and_6_out, or_3_out, ~clk);  // AND_Gate

  // Notes on the sheet:
  //   Code
  //   Data
  //   store
  //   data in
endmodule

module Op_decoder (
  input  [7:0] opcode,
  output Load,
  output Store,
  output Add,
  output With_carry,
  output Subtract,
  output Jump,
  output Hold
);

  wire equator_3_output, equator_4_output, equator_5_output, equator_6_output;

  equator equator_1 (.value1(8'h10), .value2(opcode), .\output (Load));
  equator equator_2 (.value1(8'h11), .value2(opcode), .\output (Store));
  equator equator_3 (.value1(8'h20), .value2(opcode), .\output (equator_3_output));
  equator equator_4 (.value1(8'h22), .value2(opcode), .\output (equator_4_output));
  equator equator_5 (.value1(8'h21), .value2(opcode), .\output (equator_5_output));
  equator equator_6 (.value1(8'h23), .value2(opcode), .\output (equator_6_output));
  equator equator_7 (.value1(8'h30), .value2(opcode), .\output (Jump));
  equator equator_8 (.value1({8{1'b1}}), .value2(opcode), .\output (Hold));
  or or_1 (Add, equator_3_output, equator_4_output);
  or or_2 (Subtract, equator_5_output, equator_6_output);
  or or_3 (With_carry, equator_4_output, equator_6_output);
endmodule

module equator (
  input  [7:0] value1,
  input  [7:0] value2,
  output \output 
);

  wire [7:0] xnor_1_out;

  assign xnor_1_out = ~(value1 ^ value2);  // XNOR_Gate xnor_1, 8 bits wide
  and and_1 (\output , xnor_1_out[0], xnor_1_out[1], xnor_1_out[2], xnor_1_out[3], xnor_1_out[4], xnor_1_out[5], xnor_1_out[6], xnor_1_out[7]);
endmodule

module _2bit_equator (
  input  [1:0] value1,
  input  [1:0] value2,
  output \output 
);

  wire [1:0] xnor_1_out;

  assign xnor_1_out = ~(value1 ^ value2);  // XNOR_Gate xnor_1, 2 bits wide
  and and_1 (\output , xnor_1_out[0], xnor_1_out[1]);
endmodule

module counter (
  input  [15:0] Set_value,
  input  Set,
  input  Clock,
  input  Reset,
  output [15:0] Value
);

  wire [15:0] adder_1_out, multiplexer_1_out;

  Adder #(.width(16)) adder_1 (.a(Value), .b(16'h1), .out(adder_1_out));  // open: cin, cout
  Multiplexer #(.width(16)) multiplexer_1 (.in0(adder_1_out), .in1(Set_value), .out(multiplexer_1_out), .sel(Set));
  Register #(.width(16)) register_1 (.D(multiplexer_1_out), .Q(Value), .clk(Clock), .clr(Reset));  // open: en
endmodule
